# Fritzing sketch rpi3_schematics (saved by Fritzing 0.9.3b)
circuit board: 8.46667cm x 5.64444cm
breadboards: 1

parts:
  S1 = Pushbutton [package="[THT]"]
  R1 = Resistor [tolerance=±5% resistance=10k package="0402 [SMD]"]
  Raspberry_Pi_1 = Raspberry Pi 3 [part_number=RPI-3-V1.2]

nets:
  N1: S1.Pin_1, S1.Pin_2, Raspberry_Pi_1.GND
  N2: S1.Pin_3, S1.Pin_4, R1.Pin_1, Raspberry_Pi_1.GPIO21
  N3: R1.Pin_0, Raspberry_Pi_1.5V
